# Fritzing sketch spicerack (saved by Fritzing 0.9.3b)
breadboards: 1

parts:
  BeagleBone1 = BeagleBone Black
  Part1 = EasyDriver_v44
  M1 = Stepper Motor - Bipolar
  R1 = Resistor [tolerance=±5% resistance=220 package="2512 [SMD]"]
  R2 = Resistor [tolerance=±5% resistance=220 package="2010 [SMD]"]
  LED1 = smd LED [color="Red (633nm)" package="1206 [SMD]"]
  LED2 = smd LED [color="Green (555nm)" package="1206 [SMD]"]

nets:
  N1: BeagleBone1.no_name_yet#2, LED1.cathode, LED2.cathode
  N2: BeagleBone1.no_name_yet#14, R1.Pin_1
  N3: BeagleBone1.no_name_yet#15, R2.Pin_1
  N4: BeagleBone1.no_name_yet#102, Part1.GND
  N5: BeagleBone1.no_name_yet#108, Part1.ENABLE
  N6: BeagleBone1.no_name_yet#110, Part1.MS2
  N7: BeagleBone1.no_name_yet#112, Part1.MS1
  N8: BeagleBone1.no_name_yet#114, Part1.STEP
  N9: BeagleBone1.no_name_yet#116, Part1.DIR
  N10: Part1.OUT2A, M1.A
  N11: Part1.OUT2B, M1.C
  N12: Part1.OUT1A, M1.B
  N13: Part1.OUT1B, M1.D
  N14: R1.Pin_0, LED2.anode
  N15: R2.Pin_0, LED1.anode

custom parts:
  BeagleBone Black: BeagleBone Black rev. A5B
